# Fritzing sketch cooker (saved by Fritzing 0.8.5b)
circuit board: 11.8cm x 10cm
breadboards: 1

parts:
  LCD1 = LCD screen
  R2 = Resistor [tolerance=±5% resistance=1k package=THT]
  R3 = Resistor [tolerance=±5% resistance=1k package=THT]
  R4 = Resistor [tolerance=±5% resistance=1k package=THT]
  3V3 = Battery
  ESP-01 = ESP8266 WiFi Module [part_number=ESP8266]
  BT1 = Bluetooth HC-06u [package=THT]
  R5 = Resistor [tolerance=±5% resistance=1k package=THT]
  R6 = Resistor [tolerance=±5% resistance=1k package=THT]
  R7 = Resistor [tolerance=±5% resistance=1k package=THT]
  R8 = Resistor [tolerance=±5% resistance=4.7k package=THT]
  XTAL1 = Crystal [frequency="16 Mhz" package=THT]
  ATMEGA328 = mystery part, 28 pins [chip_label=Atmega328]
  ROTARY_ENCODER = mystery part, 5 pins [chip_label=KY-040]
  C1 = Tantalum Capacitor [capacitance=20pF package="100 mil [THT, tantalum]"]
  R9 = Resistor [tolerance=±5% resistance=1k package=THT]
  C2 = Tantalum Capacitor [capacitance=20pF package="100 mil [THT, tantalum]"]
  DS1 = DS18B20 1-Wire Temperature Sensor [part_number=DS18B20]
  R10 = Resistor [tolerance=±5% resistance=1k package=THT]
  Potentiometer = Variable Capacitor [capacitance=100nF max_capacitance=10pF min_capacitance=2pF voltage=35V]
  S1 = Pushbutton [package=THT]
  LED1 = LED - 5mm [color="Red (633nm)" package="5 mm [THT]"]
  R11 = Resistor [tolerance=±5% resistance=220 package=THT]
  5V = Battery
  ASO242R = Mystery Part - 4 pins [chip_label=? package=THT]
  J1 = Screw terminal - 2 pins [package=THT]
  J2 = Screw terminal - 2 pins [package=THT]

nets:
  GND: LCD1.VSS, LCD1.LED-, R2.Pin_0, 3V3.-, ESP-01.GND, BT1.GND, R6.Pin_1, ATMEGA328.pin8, ROTARY_ENCODER.pin5, C1.-, C2.-, DS1.GND, Potentiometer.0, S1.leg1, LED1.cathode, 5V.-, ASO242R.-
  VDD: LCD1.VDD, LCD1.LED+, BT1.VCC, R8.Pin_0, ATMEGA328.pin7, ROTARY_ENCODER.pin4, R9.Pin_1, DS1.VDD, R10.Pin_0, Potentiometer.2
  N1: LCD1.V0, Potentiometer.1
  N2: LCD1.RS, ATMEGA328.pin4
  N3: LCD1.R/W, ATMEGA328.pin5
  N4: LCD1.E, ATMEGA328.pin6
  N5: LCD1.DB4, ATMEGA328.pin11
  N6: LCD1.DB5, ATMEGA328.pin12
  N7: LCD1.DB6, ATMEGA328.pin13
  N8: LCD1.DB7, ATMEGA328.pin14
  N9: R2.Pin_1, R3.Pin_1
  N10: R3.Pin_0, R4.Pin_1, ESP-01.RXD
  N11: R4.Pin_0, ATMEGA328.pin3
  N12: 3V3.+, ESP-01.VCC, ESP-01.GPIO_0, ESP-01.RST, ESP-01.GPIO_2, ESP-01.CH_PD
  N13: ESP-01.TXD, ATMEGA328.pin2
  N14: BT1.TXD, ATMEGA328.pin16
  N15: BT1.RXD, R5.Pin_0, R7.Pin_1
  N16: R5.Pin_1, R6.Pin_0
  N17: R7.Pin_0, ATMEGA328.pin15
  N18: R8.Pin_1, ATMEGA328.pin23, DS1.DQ
  N19: XTAL1.pin_0, ATMEGA328.pin10, C1.+
  N20: XTAL1.pin_1, ATMEGA328.pin9, C2.+
  N21: ATMEGA328.pin1, R10.Pin_1
  N22: ATMEGA328.pin17, ROTARY_ENCODER.pin1
  N23: ATMEGA328.pin18, ROTARY_ENCODER.pin2
  N24: ATMEGA328.pin19, ROTARY_ENCODER.pin3, R9.Pin_0
  N25: ATMEGA328.pin24, ASO242R.+
  N26: ATMEGA328.pin25, S1.leg0
  N27: ATMEGA328.pin28, R11.Pin_1
  N28: LED1.anode, R11.Pin_0
  N29: ASO242R.AC1, J2.pin1
  N30: ASO242R.AC2, J1.pin1

notes:
  Christoffer Karlsson
  ISYS16

custom parts:
  ESP8266 WiFi Module: Generic WiFi Module based on the ESP8266 with onboard PCB antenna and UART communications
  Bluetooth HC-06u: Bluetooth HC-06 - face up, pins down 16.5mm x 37.5mm PCB
  Mystery Part - 4 pins: A dummy, proxy, ersatz, stand-in part for whatever you want. With 4 pins on a 100 mil inline pin header footprint.
